// Logisim project tragamonedas.circ as structural Verilog: 11 circuits, main circuit main
module main (
  input  [1:0] Harcodeados,
  input  [1:0] Resultados,
  input  [1:0] in_3,
  output _11___Victoria,
  output out_5,
  output out_6,
  output out_7,
  output out_8,
  output out_9,
  output out_10,
  output out_11,
  output out_12,
  output out_13
);

  wire _0A, _0B, _0C, _0D, _0E, _0F, _0G, _0P, _1A, _1B, _1C, _1D, _1E, _1F, _1G, _1P, _2A, _2B, _2C, _2D,
       _2E, _2F, _2G, _2P, and_1_out, Animacion_Terminada_out, clock_1_out,
       controlador_animacion_1_display_1, controlador_animacion_1_display_2,
       controlador_animacion_1_display_3, Controlador_Creditos_hay_creditos,
       Controlador_Palanca_deteccion_palanca, Controlador_Palanca_influye, Controlador_Palanca_salida,
       Hay_premio, Jugada_aceptada, not_1_out, not_2_out, Victoria_Terminada_out;
  wire [1:0] joystick_1_y;
  wire [6:0] controlador_display_1_columna_1, controlador_display_1_columna_2,
       controlador_display_1_columna_3, controlador_display_1_columna_4, controlador_display_1_columna_5,
       controlador_display_2_columna_1, controlador_display_2_columna_2, controlador_display_2_columna_3,
       controlador_display_2_columna_4, controlador_display_2_columna_5, controlador_display_3_columna_1,
       controlador_display_3_columna_2, controlador_display_3_columna_3, controlador_display_3_columna_4,
       controlador_display_3_columna_5;
  wire [7:0] Evaluador_Premio_premio, Saldo;

  evaluador_premios Evaluador_Premio (
    .Resultado_1(in_3), .Resultado_2(Resultados), .Resultado_3(Harcodeados),
    .Premio(Evaluador_Premio_premio), .HayPremio(Hay_premio));
  Clock clock_1 (.out(clock_1_out));
  Button Victoria_Terminada (.out(Victoria_Terminada_out));
  Button Animacion_Terminada (.out(Animacion_Terminada_out));
  controlador_creditos Controlador_Creditos (
    .Jugar(Jugada_aceptada), .Premio(Evaluador_Premio_premio), .EnVictoria(Hay_premio), .Saldo_Actual(Saldo),
    .Hay_Creditos(Controlador_Creditos_hay_creditos));
  DotMatrix dotmatrix_1 (
    .col0(controlador_display_1_columna_1), .col1(controlador_display_1_columna_2),
    .col2(controlador_display_1_columna_3), .col3(controlador_display_1_columna_4),
    .col4(controlador_display_1_columna_5));
  controlador_display controlador_display_1 (
    .Resultado(Harcodeados), .Detener(controlador_animacion_1_display_1),
    .Columna_1(controlador_display_1_columna_1), .Columna_2(controlador_display_1_columna_2),
    .Columna_3(controlador_display_1_columna_3), .Columna_4(controlador_display_1_columna_4),
    .Columna_5(controlador_display_1_columna_5));
  maquina_estados maquina_estados_1 (
    .Reloj(clock_1_out), .Victoria_Terminada(Victoria_Terminada_out),
    .Nueva_Tirada(Controlador_Palanca_salida), .Hay_Creditos(Controlador_Creditos_hay_creditos),
    .Animacion_Terminada(Animacion_Terminada_out), .Hay_Premio(Hay_premio), .out_7(_11___Victoria),
    .out_8(out_5));
  DotMatrix dotmatrix_2 (
    .col0(controlador_display_2_columna_1), .col1(controlador_display_2_columna_2),
    .col2(controlador_display_2_columna_3), .col3(controlador_display_2_columna_4),
    .col4(controlador_display_2_columna_5));
  controlador_display controlador_display_2 (
    .Resultado(Resultados), .Detener(controlador_animacion_1_display_2),
    .Columna_1(controlador_display_2_columna_1), .Columna_2(controlador_display_2_columna_2),
    .Columna_3(controlador_display_2_columna_3), .Columna_4(controlador_display_2_columna_4),
    .Columna_5(controlador_display_2_columna_5));
  Joystick #(.bits(2)) joystick_1 (.y(joystick_1_y));  // open: x
  not not_1 (not_1_out, out_5);
  not not_2 (not_2_out, _11___Victoria);
  and and_1 (and_1_out, not_1_out, not_2_out, Controlador_Creditos_hay_creditos);
  visualizador_creditos visualizador_creditos_1 (
    .Saldo(Saldo), .Unidad({_0P, _0G, _0F, _0E, _0D, _0C, _0B, _0A}),
    .Decena({_1P, _1G, _1F, _1E, _1D, _1C, _1B, _1A}), .Centena({_2P, _2G, _2F, _2E, _2D, _2C, _2B, _2A}),
    .Binario({out_6, out_7, out_8, out_9, out_10, out_11, out_12, out_13}));
  controlador_palanca Controlador_Palanca (
    .Palanca(joystick_1_y), .Habilitar(and_1_out), .Salida(Controlador_Palanca_salida),
    .Influye(Controlador_Palanca_influye), .Deteccion_Palanca(Controlador_Palanca_deteccion_palanca));
  DotMatrix dotmatrix_3 (
    .col0(controlador_display_3_columna_1), .col1(controlador_display_3_columna_2),
    .col2(controlador_display_3_columna_3), .col3(controlador_display_3_columna_4),
    .col4(controlador_display_3_columna_5));
  controlador_display controlador_display_3 (
    .Resultado(in_3), .Detener(controlador_animacion_1_display_3),
    .Columna_1(controlador_display_3_columna_1), .Columna_2(controlador_display_3_columna_2),
    .Columna_3(controlador_display_3_columna_3), .Columna_4(controlador_display_3_columna_4),
    .Columna_5(controlador_display_3_columna_5));
  LED \Detección_Palanca  (.in(Controlador_Palanca_deteccion_palanca));
  LED Influye (.in(Controlador_Palanca_influye));
  controlador_animacion controlador_animacion_1 (
    .Palanca(Jugada_aceptada), .Display_1(controlador_animacion_1_display_1),
    .Display_2(controlador_animacion_1_display_2), .Display_3(controlador_animacion_1_display_3));
  and and_2 (Jugada_aceptada, Controlador_Palanca_influye, Controlador_Palanca_salida);
  _7_Segment_Display u_7_segment_display_1 (.g(_2G), .f(_2F), .a(_2A), .b(_2B), .e(_2E), .d(_2D), .c(_2C), .dp(_2P));
  _7_Segment_Display u_7_segment_display_2 (.g(_1G), .f(_1F), .a(_1A), .b(_1B), .e(_1E), .d(_1D), .c(_1C), .dp(_1P));
  _7_Segment_Display u_7_segment_display_3 (.g(_0G), .f(_0F), .a(_0A), .b(_0B), .e(_0E), .d(_0D), .c(_0C), .dp(_0P));

  // Notes on the sheet:
  //   Controlador
  //   Display
  //   Maquina de
  //   estados
  //   00 - Espera
  //   01 - Juego
  //   Controlador
  //   Display
  //   Controlador
  //   Display
  //   Controlador
  //   Animacion
endmodule

module controlador_display (
  input  [1:0] Resultado,
  input  Detener,
  output [6:0] Columna_1,
  output [6:0] Columna_2,
  output [6:0] Columna_3,
  output [6:0] Columna_4,
  output [6:0] Columna_5
);

  wire clock_1_out;
  wire [1:0] multiplexer_1_out, Simbolo_Animacion_q;

  Clock clock_1 (.out(clock_1_out));
  Counter #(.width(2), .max('h2)) Simbolo_Animacion (
    .Q(Simbolo_Animacion_q), .clk(clock_1_out));  // open: load, D, count, carry, clr
  Multiplexer #(.width(2), .enable("false")) multiplexer_1 (
    .in0(Simbolo_Animacion_q), .in1(Resultado), .out(multiplexer_1_out), .sel(Detener));
  ROM #(.addrWidth(2), .dataWidth(7)) rom_1 (.addr(multiplexer_1_out), .data(Columna_1));  // open: sel
  ROM #(.addrWidth(2), .dataWidth(7)) rom_2 (.addr(multiplexer_1_out), .data(Columna_2));  // open: sel
  ROM #(.addrWidth(2), .dataWidth(7)) rom_3 (.addr(multiplexer_1_out), .data(Columna_3));  // open: sel
  ROM #(.addrWidth(2), .dataWidth(7)) rom_4 (.addr(multiplexer_1_out), .data(Columna_4));  // open: sel
  ROM #(.addrWidth(2), .dataWidth(7)) rom_5 (.addr(multiplexer_1_out), .data(Columna_5));  // open: sel

  // Notes on the sheet:
  //   contents of rom_1 (hex, n*v repeats v):
  //   40 6 8
  //   contents of rom_2 (hex, n*v repeats v):
  //   43 3e 1b
  //   contents of rom_3 (hex, n*v repeats v):
  //   4c 7f 3e
  //   contents of rom_4 (hex, n*v repeats v):
  //   58 3e 6c
  //   contents of rom_5 (hex, n*v repeats v):
  //   60 6 8
endmodule

module controlador_palanca (
  input  [1:0] Palanca,
  input  Habilitar,
  output Deteccion_Palanca,
  output Salida,
  output Influye
);

  wire not_1_out;

  and and_1 (Deteccion_Palanca, Palanca[0], Palanca[1]);
  D_Flip_Flop d_ff_1 (
    .clk(Deteccion_Palanca), .D(1'b1), .Q(Salida), .preset(1'b0), .en(1'b1), .reset(not_1_out));  // open: Qn
  not not_1 (not_1_out, Habilitar);
  and and_2 (Influye, Salida, Habilitar);
endmodule

module controlador_animacion (
  input  Palanca,
  output Display_1,
  output Display_2,
  output Display_3
);

  wire clock_1_out, comparator_1_eq, comparator_1_gt, comparator_2_eq, comparator_2_gt, comparator_3_eq,
       comparator_3_gt;
  wire [2:0] counter_1_q;

  Counter #(.width(3), .max('h7), .ongoal("stay")) counter_1 (
    .Q(counter_1_q), .clk(clock_1_out), .clr(Palanca));  // open: load, D, count, carry
  Clock clock_1 (.out(clock_1_out));
  Comparator #(.width(3), .mode("unsigned")) comparator_1 (
    .a(counter_1_q), .b(3'b101), .gt(comparator_1_gt), .eq(comparator_1_eq));  // open: lt
  Comparator #(.width(3), .mode("unsigned")) comparator_2 (
    .a(counter_1_q), .b(3'b110), .gt(comparator_2_gt), .eq(comparator_2_eq));  // open: lt
  Comparator #(.width(3), .mode("unsigned")) comparator_3 (
    .a(counter_1_q), .b(3'b111), .gt(comparator_3_gt), .eq(comparator_3_eq));  // open: lt
  or or_1 (Display_1, comparator_1_gt, comparator_1_eq);
  or or_2 (Display_2, comparator_2_gt, comparator_2_eq);
  or or_3 (Display_3, comparator_3_gt, comparator_3_eq);

  // Notes on the sheet:
  //   Tiempo
  //   Animacion
  //   Detener 1
  //   tiempo ≥ 5
  //   Detener 2
  //   tiempo ≥ 6
  //   Detener 3
endmodule

module generador_resultados (
  input  Generar,
  input  Reloj,
  output [1:0] out_3
);

  wire and_1_out, and_2_out, comparator_1_eq, not_1_out, not_2_out, or_1_out, register_1_q;
  wire [1:0] random_1_out;

  or or_1 (or_1_out, and_2_out, Generar);
  Register #(.width(1)) register_1 (.D(or_1_out), .en(1'b1), .Q(register_1_q), .clk(Reloj));  // open: clr
  not not_1 (not_1_out, Generar);
  Random #(.width(2), .seed(1)) random_1 (.clk(Reloj), .out(random_1_out));  // open: next, clr
  and and_1 (and_1_out, register_1_q, not_1_out, not_2_out);
  Comparator #(.width(2)) comparator_1 (.a(random_1_out), .b(2'b11), .eq(comparator_1_eq));  // open: gt, lt
  and and_2 (and_2_out, register_1_q, comparator_1_eq);
  not not_2 (not_2_out, comparator_1_eq);
  Register #(.width(2)) register_2 (.D(random_1_out), .en(and_1_out), .Q(out_3), .clk(Reloj));  // open: clr

  // Notes on the sheet:
  //   Buscando
  //   Generar
endmodule

module maquina_estados (
  input  Reloj,
  input  Victoria_Terminada,
  input  Nueva_Tirada,
  input  Hay_Creditos,
  input  Animacion_Terminada,
  input  Hay_Premio,
  output out_7,
  output out_8
);

  wire and_1_out, and_2_out, and_3_out, and_4_out, and_5_out, not_1_out, not_2_out, not_3_out, not_4_out,
       not_5_out, not_6_out, not_7_out, or_1_out, or_2_out, or_3_out;

  not not_1 (not_1_out, Animacion_Terminada);
  or or_1 (or_1_out, not_1_out, Hay_Premio);
  not not_2 (not_2_out, Victoria_Terminada);
  not not_3 (not_3_out, out_7);
  not not_4 (not_4_out, out_7);
  not not_5 (not_5_out, out_8);
  not not_6 (not_6_out, out_7);
  not not_7 (not_7_out, Victoria_Terminada);
  and and_1 (and_1_out, out_7, out_8, not_2_out);
  and and_2 (and_2_out, Animacion_Terminada, Hay_Premio, out_8, not_3_out);
  and and_3 (and_3_out, not_4_out, or_1_out, out_8);
  and and_4 (and_4_out, not_5_out, not_6_out, Nueva_Tirada, Hay_Creditos);
  and and_5 (and_5_out, out_8, out_7, not_7_out);
  or or_2 (or_2_out, and_1_out, and_2_out);
  or or_3 (or_3_out, and_3_out, and_4_out, and_5_out);
  D_Flip_Flop A (.clk(Reloj), .D(or_2_out), .Q(out_7));  // open: Qn, preset, en, reset
  D_Flip_Flop B (.clk(Reloj), .D(or_3_out), .Q(out_8));  // open: Qn, preset, en, reset

  // Other names for the same wires on the sheet: R = Reloj

  // Notes on the sheet:
  //   /AT*HP
  //   B
  //   A
  //   Q  *Q  */VT
  //   AT*HP*Q  */Q
  //   B
  //   (/AT+HP)*/Q  *Q  
  //   A
  //   B
  //   /Q  */Q  *NT*HC
  //   B
  //   A
  //   Q  *Q  */VT
  //   A
  //   A
  //   B
endmodule

module control_juego (
  input  in_1,
  input  in_2
);

  // OR_Gate or_1 has open pins: in0=in_1, in1=in_2, out=open
endmodule

module controlador_creditos (
  input  Jugar,
  input  [7:0] Premio,
  input  EnVictoria,
  output [7:0] Saldo_Actual,
  output Hay_Creditos
);

  wire and_1_out, C, d_ff_1_q, inicializador_q;
  wire [7:0] adder_1_out, multiplexer_1_out, multiplexer_2_out, register_1_q, subtractor_1_out;

  Clock clock_1 (.out(C));
  Subtractor subtractor_1 (.a(Saldo_Actual), .b(8'h1), .out(subtractor_1_out));  // open: bin, bout
  Adder adder_1 (.a(Saldo_Actual), .b(Premio), .out(adder_1_out));  // open: cin, cout
  D_Flip_Flop d_ff_1 (.clk(C), .D(EnVictoria), .Q(d_ff_1_q));  // open: Qn, preset, en, reset
  Multiplexer #(.width(8)) multiplexer_1 (
    .in0(Saldo_Actual), .in1(subtractor_1_out), .out(multiplexer_1_out), .sel(Jugar), .en(1'b1));
  Multiplexer #(.width(8)) multiplexer_2 (
    .in0(multiplexer_1_out), .in1(adder_1_out), .out(multiplexer_2_out), .sel(and_1_out), .en(1'b1));
  and and_1 (and_1_out, EnVictoria, ~d_ff_1_q);  // AND_Gate
  Register register_1 (.D(multiplexer_2_out), .Q(register_1_q), .clk(C));  // open: en, clr
  Multiplexer #(.width(8)) multiplexer_3 (
    .in0(8'h3), .in1(register_1_q), .out(Saldo_Actual), .sel(inicializador_q), .en(1'b1));
  D_Flip_Flop inicializador (.clk(C), .D(1'b1), .Q(inicializador_q));  // open: Qn, preset, en, reset
  Comparator #(.mode("unsigned")) comparator_1 (.a(Saldo_Actual), .b({8{1'b0}}), .gt(Hay_Creditos));  // open: eq, lt
endmodule

module visualizador_creditos (
  input  [7:0] Saldo,
  output [7:0] Binario,
  output [7:0] Unidad,
  output [7:0] Decena,
  output [7:0] Centena
);

  wire [3:0] bitselector_1_out, bitselector_2_out, bitselector_3_out;
  wire [7:0] divider_1_out, divider_1_rem, divider_2_out, divider_2_rem;

  Divider divider_1 (.a(Saldo), .b(8'ha), .out(divider_1_out), .upper({8{1'b0}}), .rem(divider_1_rem));
  BitSelector #(.group(4)) bitselector_1 (.in(divider_1_rem), .out(bitselector_1_out), .sel(1'b0));
  Divider divider_2 (.a(divider_1_out), .b(8'ha), .out(divider_2_out), .upper({8{1'b0}}), .rem(divider_2_rem));
  digito_7_segmentos u_Unidad (.Digito(bitselector_1_out), .a__b__c__d__e__f__g__punto(Unidad));
  BitSelector #(.group(4)) bitselector_2 (.in(divider_2_rem), .out(bitselector_2_out), .sel(1'b0));
  digito_7_segmentos u_Decena (.Digito(bitselector_2_out), .a__b__c__d__e__f__g__punto(Decena));
  BitSelector #(.group(4)) bitselector_3 (.in(divider_2_out), .out(bitselector_3_out), .sel(1'b0));
  digito_7_segmentos u_Centena (.Digito(bitselector_3_out), .a__b__c__d__e__f__g__punto(Centena));
  _7_Segment_Display u_7_segment_display_1 (
    .g(Centena[6]), .f(Centena[5]), .a(Centena[0]), .b(Centena[1]), .e(Centena[4]), .d(Centena[3]),
    .c(Centena[2]), .dp(Centena[7]));
  _7_Segment_Display u_7_segment_display_2 (
    .g(Decena[6]), .f(Decena[5]), .a(Decena[0]), .b(Decena[1]), .e(Decena[4]), .d(Decena[3]), .c(Decena[2]),
    .dp(Decena[7]));
  _7_Segment_Display u_7_segment_display_3 (
    .g(Unidad[6]), .f(Unidad[5]), .a(Unidad[0]), .b(Unidad[1]), .e(Unidad[4]), .d(Unidad[3]), .c(Unidad[2]),
    .dp(Unidad[7]));

  assign Binario = Saldo;

  // Other names for the same wires on the sheet: _2A = Centena[0]; _2B = Centena[1]; _2C = Centena[2];
  //   _2D = Centena[3]; _2E = Centena[4]; _2F = Centena[5]; _2G = Centena[6]; _2P = Centena[7]; _1A = Decena[0];
  //   _1B = Decena[1]; _1C = Decena[2]; _1D = Decena[3]; _1E = Decena[4]; _1F = Decena[5]; _1G = Decena[6];
  //   _1P = Decena[7]; _0A = Unidad[0]; _0B = Unidad[1]; _0C = Unidad[2]; _0D = Unidad[3]; _0E = Unidad[4];
  //   _0F = Unidad[5]; _0G = Unidad[6]; _0P = Unidad[7]
endmodule

module digito_7_segmentos (
  input  [3:0] Digito,
  output [7:0] a__b__c__d__e__f__g__punto
);

  ROM #(.addrWidth(4)) rom_1 (.addr(Digito), .data(a__b__c__d__e__f__g__punto));  // open: sel

  // Notes on the sheet:
  //   contents of rom_1 (hex, n*v repeats v):
  //   3f 6 5b 4f 66 6d 7d 7 7f 6f
endmodule

module evaluador_premios (
  input  [1:0] Resultado_1,
  input  [1:0] Resultado_2,
  input  [1:0] Resultado_3,
  output [7:0] Premio,
  output HayPremio
);

  wire and_1_out, comparator_1_eq, comparator_2_eq;
  wire [7:0] multiplexer_1_out;

  Comparator #(.width(2)) comparator_1 (.a(Resultado_1), .b(Resultado_2), .eq(comparator_1_eq));  // open: gt, lt
  Comparator #(.width(2)) comparator_2 (.a(Resultado_2), .b(Resultado_3), .eq(comparator_2_eq));  // open: gt, lt
  Multiplexer #(.select(2), .width(8)) multiplexer_1 (
    .in0(8'h3), .in1(8'h2), .in2(8'h1), .in3({8{1'b0}}), .out(multiplexer_1_out), .sel(Resultado_1), .en(1'b1));
  and and_1 (and_1_out, comparator_1_eq, comparator_2_eq);
  Multiplexer #(.width(8)) multiplexer_2 (
    .in0({8{1'b0}}), .in1(multiplexer_1_out), .out(Premio), .sel(and_1_out), .en(1'b1));
  Comparator comparator_3 (.a(Premio), .b({8{1'b0}}), .gt(HayPremio));  // open: eq, lt

  // Notes on the sheet:
  //   Libre
  //   Campana
  //   Rayo
  //   Siete
endmodule
